# Fritzing sketch Sketch_Steckplatine (saved by Fritzing 0.9.3b)
breadboards: 1

parts:
  U1 = ESP8266 WiFi Module [part_number=ESP8266]
  R1 = Resistor [tolerance=±5% resistance=10k package="2512 [SMD]"]
  R2 = Resistor [tolerance=±5% resistance=10k package="2512 [SMD]"]
  S1 = Toggle Switch [package=THT]
  R3 = Resistor [tolerance=±5% resistance=10k package="2512 [SMD]"]
  R4 = Resistor [tolerance=±5% resistance=10k package="2512 [SMD]"]
  R5 = Resistor [tolerance=±5% resistance=1.2k package="2512 [SMD]"]
  S2 = Toggle Switch [package=THT]  # not connected

nets:
  N1: U1.VCC, R1.Pin_0, R2.Pin_0
  N2: U1.GPIO_0, S1.COM
  N3: U1.EXT_RST, R1.Pin_1
  N4: U1.GPIO_2, R4.Pin_1, R5.Pin_1
  N5: U1.CH_PD, R2.Pin_1
  N6: U1.GND, R3.Pin_0
  N7: S1.L1, R4.Pin_0
  N8: S1.L2, R3.Pin_1

custom parts:
  ESP8266 WiFi Module: Generic WiFi Module based on the ESP8266 with onboard PCB antenna and UART communications
